// Logisim project s-mips.circ as structural Verilog
module S_MIPS_Board (
  input  DESHABILITAR_DISPATCHER,
  output halt
);

  wire button_1_out, CLK, CS, d_ff_1_q, LCLR, LoadRAM, LoadRAMOn, LW, R_R_W, R_W, ram_dispatcher_1_finished,
       RCS, Reset_out, RST, TTY_EN;
  wire [2:0] KDB;
  wire [3:0] LMask, Mask, ram_1_read_time, ram_1_write_time, RMask;
  wire [6:0] KDB_DATA, TTY_DATA;
  wire [15:0] Addr, LAddr, RAddr;
  wire [31:0] I0, I1, I2, I3, LData, ram_1_data_out_0, ram_1_data_out_1, ram_1_data_out_2, ram_1_data_out_3,
       RI0, RI1, RI2, RI3;

  TTY #(.rows(25), .cols(80)) tty_1 (.data(TTY_DATA), .clk(CLK), .we(TTY_EN), .clr(RST));
  not not_1 (LoadRAMOn, ram_dispatcher_1_finished);
  RAM_Dispatcher ram_dispatcher_1 (
    .WriteTime(ram_1_write_time), .Clock(CLK), .Data(LData), .Address(LAddr), .Mask(LMask),
    .Finished(ram_dispatcher_1_finished), .Write(LW), .CLR(LCLR));
  Keyboard #(.buflen(64)) keyboard_1 (.clk(CLK), .re(KDB[0]), .avail(KDB[2]), .data(KDB_DATA));  // open: clr
  RAM_2 ram_1 (
    .Address(RAddr), .Data_Out_0(ram_1_data_out_0), .Data_Out_1(ram_1_data_out_1),
    .Data_Out_2(ram_1_data_out_2), .Data_Out_3(ram_1_data_out_3), .Data_In_0(RI0), .Data_In_1(RI1),
    .Data_In_2(RI2), .Data_In_3(RI3), .Mask(RMask), .nRead_Write(R_R_W), .Chip_Select(RCS),
    .Read_Time(ram_1_read_time), .Reset(button_1_out), .Write_Time(ram_1_write_time));
  Button button_1 (.out(button_1_out));
  D_Flip_Flop d_ff_1 (.clk(CLK), .D(1'b1), .Q(d_ff_1_q), .reset(Reset_out));  // open: Qn, preset, en
  Button Reset (.out(Reset_out));
  S_MIPS s_mips_1 (
    .Kbd_Enable(KDB[0]), .Address(Addr), .Kbd_Clear(KDB[1]), .Kbd_Available(KDB[2]), .RAM_In_0(I0),
    .Kbd_ASCII_Data(KDB_DATA), .RAM_In_1(I1), .TTY_Enable(TTY_EN), .RAM_In_2(I2), .RAM_In_3(I3),
    .TTY_ASCII_Data(TTY_DATA), .Reset(RST), .RAM_Out_0(ram_1_data_out_0), .Clock(CLK),
    .RAM_Out_1(ram_1_data_out_1), .Stop(halt), .RAM_Out_2(ram_1_data_out_2), .RAM_Out_3(ram_1_data_out_3),
    .Mask(Mask), .Read_Time(ram_1_read_time), .Write_Time(ram_1_write_time), .nRead_Write(R_W),
    .Chip_Select(CS));
  D_Flip_Flop d_ff_2 (.clk(CLK), .D(d_ff_1_q), .Qn(LCLR), .reset(Reset_out));  // open: Q, preset, en
  or or_1 (RST, LCLR, LoadRAM);
  Clock clock_1 (.out(CLK));
  Multiplexer #(.width(32), .enable("false")) multiplexer_1 (.in0(I0), .in1(LData), .out(RI0), .sel(LoadRAM));
  Multiplexer #(.width(32), .enable("false")) multiplexer_2 (.in0(I1), .in1(LData), .out(RI1), .sel(LoadRAM));
  Multiplexer #(.width(32), .enable("false")) multiplexer_3 (.in0(I2), .in1(LData), .out(RI2), .sel(LoadRAM));
  Multiplexer #(.width(32), .enable("false")) multiplexer_4 (.in0(I3), .in1(LData), .out(RI3), .sel(LoadRAM));
  and and_1 (LoadRAM, ~DESHABILITAR_DISPATCHER, LoadRAMOn);  // AND_Gate
  Multiplexer #(.width(16), .enable("false")) multiplexer_5 (.in0(Addr), .in1(LAddr), .out(RAddr), .sel(LoadRAM));
  Multiplexer #(.width(4), .enable("false")) multiplexer_6 (.in0(Mask), .in1(LMask), .out(RMask), .sel(LoadRAM));
  Multiplexer #(.enable("false")) multiplexer_7 (.in0(CS), .in1(LW), .out(RCS), .sel(LoadRAM));
  Multiplexer #(.enable("false")) multiplexer_8 (.in0(R_W), .in1(LW), .out(R_R_W), .sel(LoadRAM));

  // Notes on the sheet:
  //   NO MODIFICAR
  //   Keyboard
endmodule

module S_MIPS (
  input  Kbd_Available,
  input  [6:0] Kbd_ASCII_Data,
  input  [31:0] RAM_Out_0,
  input  [31:0] RAM_Out_1,
  input  Reset,
  input  [31:0] RAM_Out_2,
  input  Clock,
  input  [31:0] RAM_Out_3,
  input  [3:0] Read_Time,
  input  [3:0] Write_Time,
  output Kbd_Enable,
  output [15:0] Address,
  output Kbd_Clear,
  output TTY_Enable,
  output [6:0] TTY_ASCII_Data,
  output Stop,
  output [31:0] RAM_In_0,
  output [31:0] RAM_In_1,
  output [31:0] RAM_In_2,
  output [31:0] RAM_In_3,
  output [3:0] Mask,
  output nRead_Write,
  output Chip_Select
);

  wire d_ff_1_q, get_data, get_inst, InstEn, KBD, Lw, MFHI, MFLO, PCEn, Pop, Push, ready_data, ready_inst,
       ready_write, RegEn, RND, SpEn, Start, Sw, Type_I, WRITE;
  wire [5:0] Func_code, Op_code;
  wire [31:0] cur_instruction, dp_address, memory_control_1_output, memory_control_1_output_2,
       memory_control_1_output_3, memory_control_1_output_4, multiplexer_1_out, multiplexer_2_out,
       multiplexer_3_out, multiplexer_4_out, multiplexer_5_out;

  Multiplexer #(.width(32), .enable("false")) multiplexer_1 (
    .in0(RAM_Out_0), .in1(RAM_In_0), .out(multiplexer_1_out), .sel(WRITE));
  Multiplexer #(.width(32), .enable("false")) multiplexer_2 (
    .in0(RAM_Out_1), .in1(RAM_In_0), .out(multiplexer_2_out), .sel(WRITE));
  Multiplexer #(.width(32), .enable("false")) multiplexer_3 (
    .in0(RAM_Out_2), .in1(RAM_In_0), .out(multiplexer_3_out), .sel(WRITE));
  Multiplexer #(.width(32), .enable("false")) multiplexer_4 (
    .in0(RAM_Out_3), .in1(RAM_In_0), .out(multiplexer_4_out), .sel(WRITE));
  D_Flip_Flop #(.trigger("falling")) d_ff_1 (
    .clk(Clock), .D(1'b0), .Q(d_ff_1_q), .preset(Reset));  // open: Qn, en, reset
  D_Flip_Flop #(.trigger("falling")) d_ff_2 (
    .clk(Clock), .D(d_ff_1_q), .Q(Start), .reset(Reset));  // open: Qn, preset, en
  Multiplexer #(.width(32), .enable("false")) multiplexer_5 (
    .in0({32{1'b1}}), .in1({{25{1'b0}}, Kbd_ASCII_Data}), .out(multiplexer_5_out), .sel(Kbd_Available));
  Memory_Control memory_control_1 (
    .in_5(multiplexer_1_out), .in_10(multiplexer_2_out), .in_11(multiplexer_3_out),
    .in_12(multiplexer_4_out), .in_13(dp_address), .in_1(Read_Time), .in_2(Write_Time), .in_4(Reset),
    .in_6(WRITE), .in_7(get_inst), .in_8(get_data), .in_9(InstEn), .Output(memory_control_1_output),
    .Output_2(memory_control_1_output_2), .Output_3(memory_control_1_output_3),
    .Output_4(memory_control_1_output_4), .Output_5(Address), .Output_6(Mask), .Output_7(Chip_Select),
    .Output_8(nRead_Write), .Output_9(ready_inst), .Output_10(ready_data), .Output_11(ready_write),
    .in_3(Clock));
  CONTROL_UNIT control_unit_1 (
    .Start(Start), .Clock(Clock), .RST(Reset), .Op_code(Op_code), .Func_code(Func_code),
    .Ready_Inst(ready_inst), .Read_Instruction(get_inst), .Load_Instruction(InstEn), .Register_Enable(RegEn),
    .Pogram_Counter_Enable(PCEn), .Stack_Pointer_Enable(SpEn), .Type_I(Type_I), .MFHI(MFHI), .MFLO(MFLO),
    .Pop_En(Pop), .Push_En(Push), .Lw_En(Lw), .Sw_En(Sw), .KBD(KBD), .RND(RND), .Ready_Data(ready_data),
    .Read_Data(get_data), .Write_Data(WRITE), .TTY(TTY_Enable), .End(Stop), .Ready_Write(ready_write),
    .KBD_Enable(Kbd_Enable));
  DATA_PATH data_path_1 (
    .Clock(Clock), .Reset(Reset), .Instruction(cur_instruction), .KBD_Input(multiplexer_5_out),
    .Instruction_Enable(InstEn), .Type_I(Type_I), .Register_Enable(RegEn), .Program_Counter_Enable(PCEn),
    .Save_Word_Enable(Sw), .Load_Word_Enable(Lw), .MFHI(MFHI), .MFLO(MFLO), .Push(Push), .Pop(Pop),
    .SP_Write(SpEn), .RND(RND), .KBD(KBD),
    .RS___RT({RAM_In_0[7:0], RAM_In_0[15:8], RAM_In_0[23:16], RAM_In_0[31:24]}), .Memory_Address(dp_address),
    .TtyOutput(TTY_ASCII_Data), .Op_code(Op_code), .Func_code(Func_code));
  Multiplexer #(.select(2), .width(32), .enable("false")) multiplexer_6 (
    .in0(memory_control_1_output), .in1(memory_control_1_output_2), .in2(memory_control_1_output_3),
    .in3(memory_control_1_output_4), .out(cur_instruction), .sel(dp_address[3:2]));
  // Probe on cur_instruction

  assign Kbd_Clear = Reset;
  assign RAM_In_1 = RAM_In_0;
  assign RAM_In_2 = RAM_In_0;
  assign RAM_In_3 = RAM_In_0;

  // Other names for the same wires on the sheet: KBD_DATA[6:0] = Kbd_ASCII_Data; CLK = Clock; CS = Chip_Select;
  //   KBD_AVAIL = Kbd_Available; CLR = Reset; KBD_CLR = Reset; R_Out[31:0] = RAM_In_0; RAM_INPUT_0[31:0] = RAM_In_0;
  //   RAM_INPUT_1[31:0] = RAM_In_0; RAM_INPUT_2[31:0] = RAM_In_0; RAM_INPUT_3[31:0] = RAM_In_0; RAM_A[15:0] = Address;
  //   RAM_MASK[3:0] = Mask; RAM_OUTPUT_0[31:0] = RAM_Out_0; RAM_OUTPUT_1[31:0] = RAM_Out_1;
  //   RAM_OUTPUT_2[31:0] = RAM_Out_2; RAM_OUTPUT_3[31:0] = RAM_Out_3; RW = nRead_Write;
  //   TTY_DATA[6:0] = TTY_ASCII_Data

  // Notes on the sheet:
  //   RAM ADDRESS
  //   DATA FROM RAM
  //   DATA TO RAM
  //   DATA WRITE MASK
  //   RAM TIMING
  //   RAM CONTROL
  //   KEYBOARD
  //   TTY
  //   SEQUENCING
endmodule

module RAM_2 (
  input  [15:0] Address,
  input  [31:0] Data_In_0,
  input  [31:0] Data_In_1,
  input  [31:0] Data_In_2,
  input  [31:0] Data_In_3,
  input  [3:0] Mask,
  input  nRead_Write,
  input  Chip_Select,
  input  Reset,
  output [31:0] Data_Out_0,
  output [31:0] Data_Out_1,
  output [31:0] Data_Out_2,
  output [31:0] Data_Out_3,
  output [3:0] Read_Time,
  output [3:0] Write_Time
);

  wire and_2_out, and_3_out, and_4_out, and_5_out, and_6_out, and_7_out, and_8_out, and_9_out, Changed, CLK,
       comparator_2_eq, comparator_3_eq, comparator_4_eq, comparator_5_eq, comparator_6_eq, Count,
       demultiplexer_3_out0, Idle, Idle_q, Load, Load0, Load1, nand_1_out, or_1_out, or_2_out, or_3_out,
       or_4_out, or_5_out, or_6_out, or_7_out, or_8_out, or_9_out, or_10_out, Proc_q, Update_Mem, Zero_Time;
  wire [3:0] counter_1_q, multiplexer_1_out, subtractor_1_out;
  wire [31:0] register_1_q, register_2_q, register_3_q, register_4_q, register_5_q;

  // Probe on 4'b0011
  // Probe on 4'b0010
  Multiplexer #(.width(4), .enable("false")) multiplexer_1 (
    .in0(4'b0011), .in1(4'b0010), .out(multiplexer_1_out), .sel(nRead_Write));
  or or_1 (or_1_out, Idle, Update_Mem);
  or or_2 (or_2_out, ~Chip_Select, Reset);  // OR_Gate
  Subtractor #(.width(4)) subtractor_1 (.a(multiplexer_1_out), .b(4'b0010), .out(subtractor_1_out));  // open: bin, bout
  D_Flip_Flop u_Idle (.clk(CLK), .D(or_1_out), .Q(Idle_q), .preset(or_2_out));  // open: Qn, en, reset
  Demultiplexer #(.enable("false")) demultiplexer_1 (.out0(Idle), .out1(Load0), .in(Idle_q), .sel(Changed));
  // Probe on counter_1_q
  Counter #(.width(4), .max('hf)) counter_1 (
    .load(Load), .D(subtractor_1_out), .count(Count), .Q(counter_1_q), .clk(CLK), .clr(or_3_out));  // open: carry
  or or_3 (or_3_out, ~Chip_Select, Reset);  // OR_Gate
  Comparator_part #(.width(4), .mode("unsigned")) comparator_1 (
    .a(4'b0000), .b(counter_1_q), .eq(Zero_Time));  // open: gt, lt
  or or_4 (or_4_out, Count, Load0, Load1);
  Register #(.width(32)) register_1 (.D(Data_In_0), .en(Chip_Select), .Q(register_1_q), .clk(CLK), .clr(or_5_out));
  or or_5 (or_5_out, ~Chip_Select, Reset);  // OR_Gate
  Register #(.width(32)) register_2 (.D(Data_In_1), .en(Chip_Select), .Q(register_2_q), .clk(CLK), .clr(or_6_out));
  or or_6 (or_6_out, ~Chip_Select, Reset);  // OR_Gate
  Register #(.width(32)) register_3 (.D(Data_In_2), .en(Chip_Select), .Q(register_3_q), .clk(CLK), .clr(or_7_out));
  or or_7 (or_7_out, ~Chip_Select, Reset);  // OR_Gate
  Register #(.width(32)) register_4 (.D(Data_In_3), .en(Chip_Select), .Q(register_4_q), .clk(CLK), .clr(or_8_out));
  or or_8 (or_8_out, ~Chip_Select, Reset);  // OR_Gate
  Register #(.width(32)) register_5 (
    .D({{11{1'b1}}, nRead_Write, Mask, Address}), .en(Chip_Select), .Q(register_5_q), .clk(CLK),
    .clr(or_9_out));
  or or_9 (or_9_out, ~Chip_Select, Reset);  // OR_Gate
  D_Flip_Flop Proc (.clk(CLK), .D(or_4_out), .Q(Proc_q), .reset(or_10_out));  // open: Qn, preset, en
  or or_10 (or_10_out, ~Chip_Select, Reset);  // OR_Gate
  Demultiplexer #(.enable("false")) demultiplexer_2 (
    .out0(Count), .out1(Update_Mem), .in(demultiplexer_3_out0), .sel(Zero_Time));
  Demultiplexer #(.enable("false")) demultiplexer_3 (
    .out0(demultiplexer_3_out0), .out1(Load1), .in(Proc_q), .sel(Changed));
  Clock clock_1 (.out(CLK));
  Comparator_part #(.width(32)) comparator_2 (.a(register_1_q), .b(Data_In_0), .eq(comparator_2_eq));  // open: gt, lt
  Comparator_part #(.width(32)) comparator_3 (.a(register_2_q), .b(Data_In_1), .eq(comparator_3_eq));  // open: gt, lt
  Comparator_part #(.width(32)) comparator_4 (.a(register_3_q), .b(Data_In_2), .eq(comparator_4_eq));  // open: gt, lt
  Comparator_part #(.width(32)) comparator_5 (.a(register_4_q), .b(Data_In_3), .eq(comparator_5_eq));  // open: gt, lt
  Comparator_part #(.width(32)) comparator_6 (
    .a(register_5_q), .b({{11{1'b1}}, nRead_Write, Mask, Address}), .eq(comparator_6_eq));  // open: gt, lt
  nand nand_1 (nand_1_out, comparator_6_eq, comparator_2_eq, comparator_3_eq, comparator_4_eq, comparator_5_eq);
  and and_1 (Changed, nand_1_out, Chip_Select);
  or or_11 (Load, Count, Load1, Load0);
  and and_2 (and_2_out, Mask[0], Update_Mem, nRead_Write);
  and and_3 (and_3_out, Mask[1], Update_Mem, nRead_Write);
  and and_4 (and_4_out, Mask[2], Update_Mem, nRead_Write);
  and and_5 (and_5_out, Mask[3], Update_Mem, nRead_Write);
  RAM_part #(.addrWidth(16), .dataWidth(32), .bus("separate")) ram_1 (
    .addr(Address), .din(Data_In_0), .data(Data_Out_0), .str(and_2_out), .sel(Chip_Select), .clk(CLK),
    .ld(and_6_out), .clr(Reset));
  and and_6 (and_6_out, ~nRead_Write, Idle);  // AND_Gate
  RAM_part #(.addrWidth(16), .dataWidth(32), .bus("separate")) ram_2 (
    .addr(Address), .din(Data_In_1), .data(Data_Out_1), .str(and_3_out), .sel(Chip_Select), .clk(CLK),
    .ld(and_7_out), .clr(Reset));
  and and_7 (and_7_out, ~nRead_Write, Idle);  // AND_Gate
  RAM_part #(.addrWidth(16), .dataWidth(32), .bus("separate")) ram_3 (
    .addr(Address), .din(Data_In_2), .data(Data_Out_2), .str(and_4_out), .sel(Chip_Select), .clk(CLK),
    .ld(and_8_out), .clr(Reset));
  and and_8 (and_8_out, ~nRead_Write, Idle);  // AND_Gate
  RAM_part #(.addrWidth(16), .dataWidth(32), .bus("separate")) ram_4 (
    .addr(Address), .din(Data_In_3), .data(Data_Out_3), .str(and_5_out), .sel(Chip_Select), .clk(CLK),
    .ld(and_9_out), .clr(Reset));
  and and_9 (and_9_out, ~nRead_Write, Idle);  // AND_Gate

  assign Read_Time = 4'b0011;
  assign Write_Time = 4'b0010;

  // Other names for the same wires on the sheet: M0 = Mask[0]; M1 = Mask[1]; M2 = Mask[2]; M3 = Mask[3];
  //   RW = nRead_Write; CLR = Reset; CS = Chip_Select; Load2 = Count

  // Notes on the sheet:
  //   NO MODIFICAR
  //   excepto quizás los valores RT y WT
  //   BANK0
  //   BANK1
  //   BANK2
  //   BANK3
endmodule

module RAM_Dispatcher (
  input  [3:0] WriteTime,
  input  Clock,
  input  CLR,
  output [31:0] Data,
  output [15:0] Address,
  output [3:0] Mask,
  output Finished,
  output Write
);

  wire demultiplexer_2_out1, demultiplexer_3_out1, End, IDLE_q, IncAddr, Load, or_1_out, or_2_out, While_q,
       WriteEnd;
  wire [3:0] counter_1_q;
  wire [31:0] CurrentAddress_q;

  Counter #(.width(32), .max('hffffffff)) CurrentAddress (
    .count(IncAddr), .Q({CurrentAddress_q[31:18], Address, CurrentAddress_q[1:0]}), .clk(Clock), .clr(CLR));  // open: load, D, carry
  or or_1 (or_1_out, IncAddr, demultiplexer_3_out1, Finished);
  D_Flip_Flop IDLE (.clk(Clock), .D(or_1_out), .Q(IDLE_q), .preset(CLR));  // open: Qn, en, reset
  Demultiplexer #(.enable("false")) demultiplexer_1 (.out0(Load), .out1(Finished), .in(IDLE_q), .sel(End));
  D_Flip_Flop While (.clk(Clock), .D(or_2_out), .Q(While_q), .reset(CLR));  // open: Qn, preset, en
  or or_2 (or_2_out, Write, Load);
  RAM_part #(.addrWidth(18), .dataWidth(32)) ram_1 (
    .addr({Address, CurrentAddress_q[1:0]}), .data(Data), .clk(Clock));  // open: sel, ld, clr
  Demultiplexer #(.enable("false")) demultiplexer_2 (
    .out0(Write), .out1(demultiplexer_2_out1), .in(While_q), .sel(WriteEnd));
  Decoder #(.select(2)) decoder_1 (
    .out0(Mask[0]), .out1(Mask[1]), .out2(Mask[2]), .out3(Mask[3]), .sel(CurrentAddress_q[1:0]));  // open: en
  Demultiplexer #(.enable("false")) demultiplexer_3 (
    .out0(IncAddr), .out1(demultiplexer_3_out1), .in(demultiplexer_2_out1), .sel(End));
  Counter #(.width(4), .max('hf)) counter_1 (
    .load(Load), .D(WriteTime), .count(Write), .Q(counter_1_q), .clk(Clock));  // open: carry, clr
  Comparator_part #(.width(32)) comparator_1 (.a(Data), .b({32{1'b1}}), .eq(End));  // open: gt, lt
  Comparator_part #(.width(4)) comparator_2 (.a(4'b0000), .b(counter_1_q), .eq(WriteEnd));  // open: gt, lt

  // Other names for the same wires on the sheet: CLK = Clock; Count = Write; WT[3:0] = WriteTime
endmodule

module CONTROL_UNIT (
  input  Start,
  input  Clock,
  input  RST,
  input  [5:0] Op_code,
  input  [5:0] Func_code,
  input  Ready_Inst,
  input  Ready_Data,
  input  Ready_Write,
  output Read_Instruction,
  output Load_Instruction,
  output Read_Data,
  output Write_Data,
  output Register_Enable,
  output Pogram_Counter_Enable,
  output Stack_Pointer_Enable,
  output KBD_Enable,
  output Type_I,
  output MFHI,
  output MFLO,
  output Pop_En,
  output Push_En,
  output Lw_En,
  output Sw_En,
  output KBD,
  output RND,
  output TTY,
  output End
);

  wire ALU, and_1_out, and_2_out, and_3_out, comparator_1_eq, comparator_2_eq, comparator_3_eq,
       comparator_4_eq, comparator_5_eq, comparator_6_eq, comparator_9_eq, comparator_10_eq,
       comparator_11_eq, comparator_12_eq, comparator_13_eq, Cpy, demultiplexer_1_out0, demultiplexer_1_out1,
       demultiplexer_2_out0, demultiplexer_3_out0, demultiplexer_4_out0, Halt, I, IDLE_q, J, Jmp, KBD_t, Lw,
       MFHI_t, MFLO_t, Mry, or_1_out, or_2_out, or_3_out, or_6_out, or_7_out, Pop, Push, R, RND_t, SP1, SP2,
       Spc, Start_Enables, Sw, Tty_t, TtyEn, Wait_3_q, Wait_4_q, Wait_5_q, Wait_8_q, Wait_q;

  and and_1 (and_1_out, Spc, RND_t);
  and and_2 (and_2_out, Spc, KBD_t);
  and and_3 (and_3_out, Spc, Halt);
  D_Flip_Flop #(.trigger("falling")) IDLE (
    .clk(Clock), .D(demultiplexer_1_out0), .Q(IDLE_q), .preset(RST));  // open: Qn, en, reset
  Demultiplexer #(.enable("false")) demultiplexer_1 (
    .out0(demultiplexer_1_out0), .out1(demultiplexer_1_out1), .in(IDLE_q), .sel(Start));
  or or_1 (or_1_out, ALU, Cpy, Ready_Data, and_1_out, and_2_out);
  Demultiplexer #(.enable("false")) demultiplexer_2 (
    .out0(demultiplexer_2_out0), .out1(Read_Data), .in(Wait_q), .sel(or_3_out));
  D_Flip_Flop #(.trigger("falling")) Wait (.clk(Clock), .D(Mry), .Q(Wait_q), .reset(RST));  // open: Qn, preset, en
  or or_2 (or_2_out, End, and_3_out);
  D_Flip_Flop #(.trigger("falling")) Wait_2 (
    .clk(Clock), .D(or_1_out), .Q(Register_Enable), .reset(RST));  // open: Qn, preset, en
  or or_3 (or_3_out, Lw, Pop);
  D_Flip_Flop #(.trigger("falling")) u_End (.clk(Clock), .D(or_2_out), .Q(End), .reset(RST));  // open: Qn, preset, en
  or or_4 (Read_Instruction, demultiplexer_1_out1, Pogram_Counter_Enable);
  Demultiplexer #(.enable("false")) demultiplexer_3 (
    .out0(demultiplexer_3_out0), .out1(SP2), .in(demultiplexer_2_out0), .sel(Push));
  Demultiplexer #(.enable("false")) demultiplexer_4 (.out0(demultiplexer_4_out0), .out1(SP1), .in(Wait_3_q), .sel(Pop));
  D_Flip_Flop #(.trigger("falling")) Wait_3 (
    .clk(Clock), .D(Register_Enable), .Q(Wait_3_q), .reset(RST));  // open: Qn, preset, en
  and and_4 (TtyEn, Spc, Tty_t);
  and and_5 (KBD_Enable, KBD_t, demultiplexer_4_out0);
  or or_5 (Write_Data, demultiplexer_3_out0, Wait_4_q);
  D_Flip_Flop #(.trigger("falling")) Wait_4 (.clk(Clock), .D(SP2), .Q(Wait_4_q), .reset(RST));  // open: Qn, preset, en
  or or_6 (or_6_out, demultiplexer_4_out0, Wait_5_q);
  D_Flip_Flop #(.trigger("falling")) Wait_5 (.clk(Clock), .D(SP1), .Q(Wait_5_q), .reset(RST));  // open: Qn, preset, en
  D_Flip_Flop #(.trigger("falling")) Wait_6 (
    .clk(Clock), .D(Ready_Inst), .Q(Start_Enables), .reset(RST));  // open: Qn, preset, en
  D_Flip_Flop #(.trigger("falling")) Wait_7 (
    .clk(Clock), .D(or_7_out), .Q(Pogram_Counter_Enable), .reset(RST));  // open: Qn, preset, en
  or or_7 (or_7_out, or_6_out, Jmp, Ready_Write, TtyEn);
  Operation_Decoder operation_decoder_1 (
    .Op_code(Op_code), .Func_code(Func_code), .Type_R(R), .Type_I(I), .Type_J(J), .Copy_Inst(Cpy),
    .Jump_Inst(Jmp), .Memory_Inst(Mry), .Special_Inst(Spc), .ALU_Inst(ALU), .Enable(Start_Enables));
  Comparator_part #(.width(6)) comparator_1 (.a(Op_code), .b({6{1'b0}}), .eq(comparator_1_eq));  // open: gt, lt
  Comparator_part #(.width(6)) comparator_2 (.a(Func_code), .b(6'b010010), .eq(comparator_2_eq));  // open: gt, lt
  and and_6 (MFLO_t, comparator_2_eq, comparator_1_eq);
  and and_7 (MFHI_t, comparator_1_eq, comparator_3_eq);
  Comparator_part #(.width(6)) comparator_3 (.a(Func_code), .b(6'b010000), .eq(comparator_3_eq));  // open: gt, lt
  Comparator_part #(.width(6)) comparator_4 (.a(Op_code), .b(6'b111000), .eq(comparator_4_eq));  // open: gt, lt
  and and_8 (Pop, comparator_4_eq, comparator_5_eq);
  Comparator_part #(.width(6)) comparator_5 (.a(Func_code), .b({6{1'b0}}), .eq(comparator_5_eq));  // open: gt, lt
  and and_9 (Push, comparator_4_eq, comparator_6_eq);
  Comparator_part #(.width(6)) comparator_6 (.a(Func_code), .b(6'b000001), .eq(comparator_6_eq));  // open: gt, lt
  Comparator_part #(.width(6)) comparator_7 (.a(Op_code), .b(6'b100011), .eq(Lw));  // open: gt, lt
  Comparator_part #(.width(6)) comparator_8 (.a(Op_code), .b(6'b101011), .eq(Sw));  // open: gt, lt
  Comparator_part #(.width(6)) comparator_9 (.a(Op_code), .b({6{1'b1}}), .eq(comparator_9_eq));  // open: gt, lt
  and and_10 (RND_t, comparator_9_eq, comparator_10_eq);
  Comparator_part #(.width(6)) comparator_10 (.a(Func_code), .b(6'b000010), .eq(comparator_10_eq));  // open: gt, lt
  and and_11 (KBD_t, comparator_9_eq, comparator_11_eq);
  Comparator_part #(.width(6)) comparator_11 (.a(Func_code), .b(6'b000100), .eq(comparator_11_eq));  // open: gt, lt
  and and_12 (Tty_t, comparator_9_eq, comparator_12_eq);
  Comparator_part #(.width(6)) comparator_12 (.a(Func_code), .b(6'b000001), .eq(comparator_12_eq));  // open: gt, lt
  and and_13 (Halt, comparator_9_eq, comparator_13_eq);
  Comparator_part #(.width(6)) comparator_13 (.a(Func_code), .b({6{1'b1}}), .eq(comparator_13_eq));  // open: gt, lt
  or or_8 (Stack_Pointer_Enable, SP2, SP1);
  and and_14 (Type_I, I, Wait_8_q);
  and and_15 (MFHI, MFHI_t, Wait_8_q);
  and and_16 (MFLO, MFLO_t, Wait_8_q);
  and and_17 (Pop_En, Pop, Wait_8_q);
  and and_18 (Push_En, Push, Wait_8_q);
  and and_19 (Lw_En, Lw, Wait_8_q);
  and and_20 (Sw_En, Sw, Wait_8_q);
  and and_21 (KBD, KBD_t, Wait_8_q);
  and and_22 (RND, RND_t, Wait_8_q);
  and and_23 (TTY, TtyEn, Wait_8_q);
  D_Flip_Flop #(.trigger("falling")) Wait_8 (
    .clk(Clock), .Q(Wait_8_q), .preset(Start_Enables), .reset(Pogram_Counter_Enable));  // open: D, Qn, en

  assign Load_Instruction = Ready_Inst;

  // Other names for the same wires on the sheet: CLK = Clock; CLR = RST; Load_Inst = Ready_Inst;
  //   Read_Inst = Read_Instruction; RegEN = Register_Enable; SPEN = Stack_Pointer_Enable;
  //   PCEN = Pogram_Counter_Enable; Stop_Enables = Pogram_Counter_Enable

  // Notes on the sheet:
  //   Flags
endmodule

module Operation_Decoder (
  input  [5:0] Op_code,
  input  [5:0] Func_code,
  input  Enable,
  output Type_R,
  output Type_I,
  output Type_J,
  output Copy_Inst,
  output Jump_Inst,
  output Memory_Inst,
  output Special_Inst,
  output ALU_Inst
);

  wire _000000, _111000, _111111, and_3_out, and_4_out, and_5_out, and_6_out, and_7_out, comparator_1_eq,
       comparator_5_eq, comparator_6_eq, comparator_7_eq, comparator_8_eq, comparator_9_lt, comparator_10_eq,
       comparator_11_eq, nor_1_out, not_1_out, not_2_out, or_2_out, or_3_out, or_4_out;

  not not_1 (not_1_out, Type_R);
  not not_2 (not_2_out, comparator_1_eq);
  Comparator_part #(.width(6)) comparator_1 (.a(Op_code), .b(6'b000010), .eq(comparator_1_eq));  // open: gt, lt
  or or_1 (Type_R, _000000, _111000, _111111);
  and and_1 (Type_I, not_2_out, not_1_out);
  and and_2 (Type_J, comparator_1_eq, not_1_out);
  Comparator_part #(.width(6)) comparator_2 (.a(Op_code), .b({6{1'b0}}), .eq(_000000));  // open: gt, lt
  Comparator_part #(.width(6)) comparator_3 (.a(Op_code), .b(6'b111000), .eq(_111000));  // open: gt, lt
  Comparator_part #(.width(6)) comparator_4 (.a(Op_code), .b({6{1'b1}}), .eq(_111111));  // open: gt, lt
  Comparator_part #(.width(6)) comparator_5 (.a(Func_code), .b(6'b010010), .eq(comparator_5_eq));  // open: gt, lt
  and and_3 (and_3_out, comparator_5_eq, _000000);
  and and_4 (and_4_out, _000000, comparator_6_eq);
  Comparator_part #(.width(6)) comparator_6 (.a(Func_code), .b(6'b010000), .eq(comparator_6_eq));  // open: gt, lt
  Comparator_part #(.width(6)) comparator_7 (.a(Func_code), .b({6{1'b0}}), .eq(comparator_7_eq));  // open: gt, lt
  and and_5 (and_5_out, comparator_7_eq, _000000);
  and and_6 (and_6_out, _000000, comparator_8_eq);
  Comparator_part #(.width(6)) comparator_8 (.a(Func_code), .b(6'b001000), .eq(comparator_8_eq));  // open: gt, lt
  Comparator_part #(.width(6), .mode("unsigned")) comparator_9 (
    .a(Op_code), .b(6'b001000), .lt(comparator_9_lt));  // open: gt, eq
  and and_7 (and_7_out, comparator_9_lt, Type_I);
  Comparator_part #(.width(6)) comparator_10 (.a(Op_code), .b(6'b100011), .eq(comparator_10_eq));  // open: gt, lt
  Comparator_part #(.width(6)) comparator_11 (.a(Op_code), .b(6'b101011), .eq(comparator_11_eq));  // open: gt, lt
  or or_2 (or_2_out, and_3_out, and_4_out);
  or or_3 (or_3_out, and_5_out, and_6_out, and_7_out);
  or or_4 (or_4_out, _111000, comparator_10_eq, comparator_11_eq);
  and and_8 (Copy_Inst, Enable, or_2_out);
  and and_9 (Jump_Inst, Enable, or_3_out);
  and and_10 (Memory_Inst, Enable, or_4_out);
  and and_11 (Special_Inst, Enable, _111111);
  and and_12 (ALU_Inst, Enable, nor_1_out);
  nor nor_1 (nor_1_out, Copy_Inst, Jump_Inst, Memory_Inst, Special_Inst);

  // Other names for the same wires on the sheet: EN = Enable
endmodule

module DATA_PATH (
  input  Clock,
  input  [31:0] KBD_Input,
  input  Reset,
  input  [31:0] Instruction,
  input  Instruction_Enable,
  input  Type_I,
  input  Register_Enable,
  input  Program_Counter_Enable,
  input  Save_Word_Enable,
  input  Load_Word_Enable,
  input  MFHI,
  input  MFLO,
  input  Push,
  input  Pop,
  input  SP_Write,
  input  RND,
  input  KBD,
  output [5:0] Op_code,
  output [5:0] Func_code,
  output [31:0] RS___RT,
  output [31:0] Memory_Address,
  output [6:0] TtyOutput
);

  wire Sign;
  wire [3:0] alu_control_1_selector;
  wire [4:0] multiplexer_2_out, RD, RS, RT;
  wire [15:0] Const;
  wire [25:0] Destine;
  wire [31:0] ALUOut, Const_star, Hi, instruction_1_output, Lo, multiplexer_1_out, PC, PC_star, random_1_out,
       RT_t, SP;
  wire [31:7] RS_t;

  Instruction instruction_1 (
    .Input(Instruction), .CLK(Clock), .RST(Reset), .EN(Instruction_Enable), .Output(instruction_1_output));
  Program_Counter program_counter_1 (
    .Input(PC_star), .Clock(Clock), .Reset(Reset), .Enable(Program_Counter_Enable), .Output(PC));
  Branch_Control branch_control_1 (
    .Instruction_Address(PC), .Destine(Destine), .Offset(Const), .RS({RS_t, TtyOutput}), .RT(RT_t),
    .Next_Instruction_Address(PC_star), .Op_code(Op_code), .Func_code(Func_code));
  Instruction_Decoder instruction_decoder_1 (
    .Instruction(instruction_1_output), .RS(RS), .RT(RT), .RD(RD), .Destine(Destine), .Constant(Const),
    .Op_code(Op_code), .Func_code(Func_code));
  Multiplexer #(.width(32), .enable("false")) multiplexer_1 (
    .in0(RT_t), .in1(Const_star), .out(multiplexer_1_out), .sel(Type_I));
  Random #(.width(32)) random_1 (.clk(Clock), .out(random_1_out));  // open: next, clr
  ALU alu_1 (
    .in_4(Sign), .Input({RS_t, TtyOutput}), .Input_2(multiplexer_1_out), .in_3(alu_control_1_selector),
    .Output(ALUOut), .LO(Lo), .HI(Hi), .in_5(Clock));
  ALU_Control alu_control_1 (
    .Op_code(Op_code), .Func_code(Func_code), .Sign(Sign), .Selector(alu_control_1_selector), .Const(Const),
    .Const_Extended(Const_star));
  Multiplexer #(.width(5), .enable("false")) multiplexer_2 (.in0(RD), .in1(RT), .out(multiplexer_2_out), .sel(Type_I));
  Register_File register_file_1 (
    .in_14(Reset), .in_17(Register_Enable), .in_11(Push), .in_15(Clock), .in_12(SP_Write),
    .in_18(multiplexer_2_out), .in_19(RS), .in_20(RT), .Output({RS_t, TtyOutput}), .Output_2(RT_t),
    .Output_3(SP), .in_2(ALUOut), .in_3(Load_Word_Enable), .in_6(random_1_out), .in_5(MFHI), .in_7(MFLO),
    .in_9(Instruction), .in_8(RND), .in_10(KBD), .HI(Hi), .LO(Lo), .in_4(Pop), .KBD_Input(KBD_Input));
  Multiplexer #(.width(32), .enable("false")) multiplexer_3 (
    .in0({RS_t, TtyOutput}), .in1(RT_t), .out(RS___RT), .sel(Save_Word_Enable));
  Memory_Address memory_address_1 (
    .Program_Counter(PC), .Stack_Pointer(SP), .ALU_Result(ALUOut), .Address(Memory_Address), .Push(Push),
    .Pop(Pop), .Lw(Load_Word_Enable), .Sw(Save_Word_Enable));

  // Other names for the same wires on the sheet: CLK = Clock; CLR = Reset; I = Type_I; InstEN = Instruction_Enable;
  //   LwEN = Load_Word_Enable; PCEN = Program_Counter_Enable; RegEN = Register_Enable; RS_t[6:0] = TtyOutput;
  //   SwEN = Save_Word_Enable

  // Notes on the sheet:
  //   Flags
endmodule

module ALU (
  input  [31:0] Input,
  input  [31:0] Input_2,
  input  [3:0] in_3,
  input  in_4,
  input  in_5,
  output [31:0] Output,
  output [31:0] LO,
  output [31:0] HI
);

  wire div, enable, mul;
  wire [31:0] add, \and , div_rem, div_res, mul_HI, mul_LO, multiplexer_2_out, multiplexer_3_out, \nand ,
       \nor , \or , slt, sub, \xor ;

  assign \and  = Input & Input_2;  // AND_Gate and_1, 32 bits wide
  assign \or  = Input | Input_2;  // OR_Gate or_1, 32 bits wide
  assign \nand  = ~(Input & Input_2);  // NAND_Gate nand_1, 32 bits wide
  assign \nor  = ~(Input | Input_2);  // NOR_Gate nor_1, 32 bits wide
  assign \xor  = Input ^ Input_2;  // XOR_Gate xor_1, 32 bits wide
  Adder #(.width(32)) adder_1 (.a(Input), .b(Input_2), .out(add));  // open: cin, cout
  Subtractor #(.width(32)) subtractor_1 (.a(Input), .b(Input_2), .out(sub));  // open: bin, bout
  Divider divider_1 (.in_1(Input), .in_3(in_4), .in_2(Input_2), .Result(div_res), .Remainder(div_rem));
  Multiplier multiplier_1 (.in_1(Input), .in_3(in_4), .in_2(Input_2), .Output(mul_HI), .Output_2(mul_LO));
  Comparator comparator_1 (.in_1(Input), .in_3(in_4), .in_2(Input_2), .Output(slt));
  Multiplexer #(.select(4), .width(32), .enable("false")) multiplexer_1 (
    .in0(add), .in1(sub), .in4(slt), .in5(\and ), .in6(\or ), .in7(\nor ), .in8(\xor ), .out(Output),
    .sel(in_3));  // open: in2, in3, in9, in10, in11, in12, in13, in14, in15
  and and_2 (mul, ~in_3[0], in_3[1], ~in_3[2], ~in_3[3]);  // AND_Gate
  and and_3 (div, in_3[0], in_3[1], ~in_3[2], ~in_3[3]);  // AND_Gate
  or or_2 (enable, mul, div);
  Multiplexer #(.width(32), .enable("false")) multiplexer_2 (
    .in0(mul_LO), .in1(div_res), .out(multiplexer_2_out), .sel(div));
  Multiplexer #(.width(32), .enable("false")) multiplexer_3 (
    .in0(mul_HI), .in1(div_rem), .out(multiplexer_3_out), .sel(div));
  Register #(.width(32)) register_1 (.D(multiplexer_2_out), .en(enable), .Q(LO), .clk(in_5));  // open: clr
  Register #(.width(32)) register_2 (.D(multiplexer_3_out), .en(enable), .Q(HI), .clk(in_5));  // open: clr

  // Other names for the same wires on the sheet: a[31:0] = Input; b[31:0] = Input_2; clock = in_5; _0 = in_3[0];
  //   selector[3:0] = in_3; _1 = in_3[1]; _2 = in_3[2]; _3 = in_3[3]; sign = in_4
endmodule

module ALU_Control (
  input  [15:0] Const,
  input  [5:0] Op_code,
  input  [5:0] Func_code,
  output Sign,
  output [3:0] Selector,
  output [31:0] Const_Extended
);

  wire Add, AddI, And, AndI, comparator_1_eq, comparator_2_eq, comparator_3_eq, comparator_4_eq,
       comparator_5_eq, comparator_6_eq, comparator_7_eq, comparator_8_eq, comparator_9_eq, comparator_10_eq,
       comparator_11_eq, comparator_12_eq, comparator_13_eq, Div, DivU, Lw, Mult, MultU, Nor, Or, or_1_out,
       OrI, Slt, SltU, StlI, StlIU, Sub, Sw, Xor, XorI;

  Comparator_part #(.width(6)) comparator_1 (.a(Op_code), .b({6{1'b0}}), .eq(comparator_1_eq));  // open: gt, lt
  Comparator_part #(.width(6)) comparator_2 (.a(Func_code), .b(6'b100000), .eq(comparator_2_eq));  // open: gt, lt
  Comparator_part #(.width(6)) comparator_3 (.a(Func_code), .b(6'b100010), .eq(comparator_3_eq));  // open: gt, lt
  Comparator_part #(.width(6)) comparator_4 (.a(Func_code), .b(6'b011000), .eq(comparator_4_eq));  // open: gt, lt
  Comparator_part #(.width(6)) comparator_5 (.a(Func_code), .b(6'b011001), .eq(comparator_5_eq));  // open: gt, lt
  Comparator_part #(.width(6)) comparator_6 (.a(Func_code), .b(6'b011010), .eq(comparator_6_eq));  // open: gt, lt
  Comparator_part #(.width(6)) comparator_7 (.a(Func_code), .b(6'b011011), .eq(comparator_7_eq));  // open: gt, lt
  Comparator_part #(.width(6)) comparator_8 (.a(Func_code), .b(6'b100100), .eq(comparator_8_eq));  // open: gt, lt
  Comparator_part #(.width(6)) comparator_9 (.a(Func_code), .b(6'b100101), .eq(comparator_9_eq));  // open: gt, lt
  Comparator_part #(.width(6)) comparator_10 (.a(Func_code), .b(6'b100111), .eq(comparator_10_eq));  // open: gt, lt
  Comparator_part #(.width(6)) comparator_11 (.a(Func_code), .b(6'b101000), .eq(comparator_11_eq));  // open: gt, lt
  Comparator_part #(.width(6)) comparator_12 (.a(Func_code), .b(6'b101010), .eq(comparator_12_eq));  // open: gt, lt
  Comparator_part #(.width(6)) comparator_13 (.a(Func_code), .b(6'b101011), .eq(comparator_13_eq));  // open: gt, lt
  and and_1 (Add, comparator_1_eq, comparator_2_eq);
  and and_2 (Sub, comparator_1_eq, comparator_3_eq);
  and and_3 (Mult, comparator_1_eq, comparator_4_eq);
  and and_4 (MultU, comparator_1_eq, comparator_5_eq);
  and and_5 (Div, comparator_1_eq, comparator_6_eq);
  and and_6 (DivU, comparator_1_eq, comparator_7_eq);
  and and_7 (And, comparator_1_eq, comparator_8_eq);
  and and_8 (Or, comparator_1_eq, comparator_9_eq);
  and and_9 (Nor, comparator_1_eq, comparator_10_eq);
  and and_10 (Xor, comparator_1_eq, comparator_11_eq);
  and and_11 (Slt, comparator_1_eq, comparator_12_eq);
  and and_12 (SltU, comparator_1_eq, comparator_13_eq);
  Comparator_part #(.width(6)) comparator_14 (.a(Op_code), .b(6'b001000), .eq(AddI));  // open: gt, lt
  Comparator_part #(.width(6)) comparator_15 (.a(Op_code), .b(6'b001100), .eq(AndI));  // open: gt, lt
  Comparator_part #(.width(6)) comparator_16 (.a(Op_code), .b(6'b001101), .eq(OrI));  // open: gt, lt
  Comparator_part #(.width(6)) comparator_17 (.a(Op_code), .b(6'b001110), .eq(XorI));  // open: gt, lt
  Comparator_part #(.width(6)) comparator_18 (.a(Op_code), .b(6'b001010), .eq(StlI));  // open: gt, lt
  Comparator_part #(.width(6)) comparator_19 (.a(Op_code), .b(6'b001011), .eq(StlIU));  // open: gt, lt
  Comparator_part #(.width(6)) comparator_20 (.a(Op_code), .b(6'b100011), .eq(Lw));  // open: gt, lt
  Comparator_part #(.width(6)) comparator_21 (.a(Op_code), .b(6'b101011), .eq(Sw));  // open: gt, lt
  or or_1 (or_1_out, Lw, AddI, Sw);
  and and_13 (Const_Extended[31], Const[15], ~AndI, ~OrI, ~XorI);  // AND_Gate
  ALU_Encoder alu_encoder_1 (
    .in_1(Add), .in_2(Sub), .in_3(Mult), .in_4(MultU), .in_5(Div), .in_6(DivU), .in_7(Slt), .in_8(SltU),
    .in_9(And), .in_10(Or), .in_11(Nor), .in_12(Xor), .in_13(or_1_out), .in_14(StlI), .in_15(StlIU),
    .in_16(AndI), .in_17(OrI), .in_18(XorI), .sign(Sign), .selector(Selector));  // open: I

  assign Const_Extended[30:0] = {{15{Const_Extended[31]}}, Const};
endmodule

module ALU_Encoder (
  input  in_1,
  input  in_2,
  input  in_3,
  input  in_4,
  input  in_5,
  input  in_6,
  input  in_7,
  input  in_8,
  input  in_9,
  input  in_10,
  input  in_11,
  input  in_12,
  input  in_13,
  input  in_14,
  input  in_15,
  input  in_16,
  input  in_17,
  input  in_18,
  output sign,
  output I,
  output [3:0] selector
);

  wire AND, DIV, MUL, OR, SLT, SLTI;

  or or_1 (MUL, in_3, in_4);
  or or_2 (DIV, in_5, in_6);
  or or_3 (SLT, in_7, in_8);
  or or_4 (SLTI, in_14, in_15);
  or or_5 (AND, in_9, in_16);
  or or_6 (OR, in_10, in_17);
  or or_7 (selector[3], in_12, in_18);
  or or_8 (selector[0], in_2, DIV, AND, in_11);
  or or_9 (selector[1], MUL, DIV, OR, in_11);
  or or_10 (selector[2], SLT, SLTI, OR, AND, in_11);
  or or_11 (sign, in_3, in_5, in_7, in_14);
  or or_12 (I, in_13, SLTI, in_16, in_17, in_18);

  // Other names for the same wires on the sheet: add = in_1; addi = in_13; and_t = in_9; andi = in_16; div_t = in_5;
  //   divu = in_6; mul_t = in_3; mulu = in_4; nor = in_11; or_t = in_10; ori = in_17; _0 = selector[0];
  //   _1 = selector[1]; _2 = selector[2]; _3 = selector[3]; XOR = selector[3]; slt_t = in_7; slti_t = in_14;
  //   sltiu = in_15; sltu = in_8; sub = in_2; xor_t = in_12; xori = in_18
endmodule

module Comparator (
  input  [31:0] in_1,
  input  [31:0] in_2,
  input  in_3,
  output [31:0] Output
);

  wire multiplexer_1_out, slt, sltu;

  Comparator_part #(.width(32)) comparator_1 (.a(in_1), .b(in_2), .lt(slt));  // open: gt, eq
  Comparator_part #(.width(32), .mode("unsigned")) comparator_2 (.a(in_1), .b(in_2), .lt(sltu));  // open: gt, eq
  Multiplexer #(.enable("false")) multiplexer_1 (.in0(sltu), .in1(slt), .out(multiplexer_1_out), .sel(in_3));
  assign Output = {{31{1'b0}}, multiplexer_1_out};  // Bit_Extender bit_extender_1

  // Other names for the same wires on the sheet: a[31:0] = in_1; b[31:0] = in_2; sign = in_3
endmodule

module Divider (
  input  [31:0] in_1,
  input  [31:0] in_2,
  input  in_3,
  output [31:0] Result,
  output [31:0] Remainder
);

  wire negative_a, negative_b, negative_result;
  wire [31:0] abs_a, abs_b, abs_result, adder_1_out, divider_1_out, multiplexer_1_out, negator_1_out,
       negator_2_out, negator_3_out, negator_4_out, rem, subtractor_1_out;

  Divider_part #(.width(32)) divider_1 (.a(abs_a), .b(abs_b), .out(divider_1_out), .rem(rem));  // open: upper
  xor xor_1 (negative_result, negative_a, negative_b);
  and and_1 (negative_a, in_1[31], in_3);
  and and_2 (negative_b, in_3, in_2[31]);
  Adder #(.width(32)) adder_1 (.a(divider_1_out), .b(32'h1), .out(adder_1_out));  // open: cin, cout
  Multiplexer #(.width(32), .enable("false")) multiplexer_1 (
    .in0(divider_1_out), .in1(adder_1_out), .out(multiplexer_1_out), .sel(negative_a));
  Negator #(.width(32)) negator_1 (.in(in_1), .out(negator_1_out));
  Negator #(.width(32)) negator_2 (.in(in_2), .out(negator_2_out));
  Multiplexer #(.width(32), .enable("false")) multiplexer_2 (
    .in0(multiplexer_1_out), .in1(negator_3_out), .out(Result), .sel(negative_result));
  Negator #(.width(32)) negator_3 (.in(multiplexer_1_out), .out(negator_3_out));
  Negator #(.width(32)) negator_4 (.in(abs_result), .out(negator_4_out));
  Multiplexer #(.width(32), .enable("false")) multiplexer_3 (
    .in0(in_1), .in1(negator_1_out), .out(abs_a), .sel(negative_a));
  Multiplexer #(.width(32), .enable("false")) multiplexer_4 (
    .in0(in_2), .in1(negator_2_out), .out(abs_b), .sel(negative_b));
  Multiplexer #(.width(32), .enable("false")) multiplexer_5 (
    .in0(abs_result), .in1(negator_4_out), .out(Result), .sel(negative_result));
  Subtractor #(.width(32)) subtractor_1 (.a(abs_b), .b(rem), .out(subtractor_1_out));  // open: bin, bout
  Multiplexer #(.width(32), .enable("false")) multiplexer_6 (
    .in0(rem), .in1(subtractor_1_out), .out(Remainder), .sel(negative_a));

  // Other names for the same wires on the sheet: a[31:0] = in_1; b[31:0] = in_2; sign = in_3
endmodule

module Multiplier (
  input  [31:0] in_1,
  input  [31:0] in_2,
  input  in_3,
  output [31:0] Output,
  output [31:0] Output_2
);

  wire adder_1_cout, adder_3_cout, adder_5_cout, and_2_out, c1, c2, ca, cb;
  wire [31:0] a_2, a_cb, adder_1_out, adder_2_out, adder_3_out, adder_4_out, and_1_out, and_3_out, b_2, b_ca,
       bit_extender_1_out, bit_extender_2_out, c_ab, HI, HIU, LO, LOU, multiplier_1_cout, multiplier_1_out,
       shift_left_3_out_3, shift_left_4_out_3, shift_left_5_out_3, shift_left_out_3;

  Shift_Right shift_right_1 (.in_1(in_1), .out_4(a_2), .Output(ca), .in_2(1'b0));
  assign and_1_out = a_2 & bit_extender_1_out;  // AND_Gate and_1, 32 bits wide
  assign bit_extender_1_out = {{31{cb}}, cb};  // Bit_Extender bit_extender_1
  Multiplier_part #(.width(32)) multiplier_1 (
    .a(a_2), .b(b_2), .out(multiplier_1_out), .cout(multiplier_1_cout));  // open: cin
  Shift_Left shift_left (.in_2(multiplier_1_out), .out_3(shift_left_out_3), .Output(c1), .in_1(1'b0));
  Shift_Right shift_right_2 (.in_1(in_2), .out_4(b_2), .Output(cb), .in_2(1'b0));
  Shift_Left shift_left_2 (.in_2(and_1_out), .out_3(a_cb), .in_1(1'b0));  // open: Output
  Shift_Left shift_left_3 (.in_2(shift_left_out_3), .out_3(shift_left_3_out_3), .Output(c2), .in_1(1'b0));
  Shift_Left shift_left_4 (.in_2(multiplier_1_cout), .out_3(shift_left_4_out_3), .in_1(c1));  // open: Output
  Shift_Left shift_left_5 (.in_2(shift_left_4_out_3), .out_3(shift_left_5_out_3), .in_1(c2));  // open: Output
  and and_2 (and_2_out, ca, cb);
  assign bit_extender_2_out = {{31{ca}}, ca};  // Bit_Extender bit_extender_2
  Adder #(.width(32)) adder_1 (.a(shift_left_3_out_3), .b(a_cb), .out(adder_1_out), .cout(adder_1_cout));  // open: cin
  Adder #(.width(32)) adder_2 (
    .a(shift_left_5_out_3), .b({32{1'b0}}), .out(adder_2_out), .cin(adder_1_cout));  // open: cout
  assign c_ab = {{31{1'b0}}, and_2_out};  // Bit_Extender bit_extender_3
  assign and_3_out = b_2 & bit_extender_2_out;  // AND_Gate and_3, 32 bits wide
  Adder #(.width(32)) adder_3 (.a(adder_1_out), .b(b_ca), .out(adder_3_out), .cout(adder_3_cout));  // open: cin
  Adder #(.width(32)) adder_4 (.a(adder_2_out), .b({32{1'b0}}), .out(adder_4_out), .cin(adder_3_cout));  // open: cout
  Shift_Left shift_left_6 (.in_2(and_3_out), .out_3(b_ca), .in_1(1'b0));  // open: Output
  Adder #(.width(32)) adder_5 (.a(adder_3_out), .b(c_ab), .out(LOU), .cout(adder_5_cout));  // open: cin
  Adder #(.width(32)) adder_6 (.a(adder_4_out), .b({32{1'b0}}), .out(HIU), .cin(adder_5_cout));  // open: cout
  Multiplexer #(.width(32), .enable("false")) multiplexer_1 (.in0(HIU), .in1(HI), .out(Output), .sel(in_3));
  Multiplexer #(.width(32), .enable("false")) multiplexer_2 (.in0(LOU), .in1(LO), .out(Output_2), .sel(in_3));
  Multiplier_part #(.width(32)) multiplier_2 (.a(in_1), .b(in_2), .out(LO), .cout(HI));  // open: cin

  // Other names for the same wires on the sheet: a[31:0] = in_1; b[31:0] = in_2; sign = in_3
endmodule

module Shift_Right (
  input  [31:0] in_1,
  input  in_2,
  output Output,
  output [31:0] out_4
);


  assign out_4 = {in_2, in_1[31:1]};
  assign Output = in_1[0];

  // Other names for the same wires on the sheet: a[31:0] = in_1; a____1[31:0] = {in_2, in_1[31:1]}
endmodule

module Shift_Left (
  input  in_1,
  input  [31:0] in_2,
  output [31:0] out_3,
  output Output
);


  assign out_3 = {in_2[30:0], in_1};
  assign Output = in_2[31];

  // Other names for the same wires on the sheet: a[31:0] = in_2; a____1[31:0] = {in_2[30:0], in_1}
endmodule

module Register_File (
  input  [31:0] KBD_Input,
  input  [31:0] in_2,
  input  in_3,
  input  in_4,
  input  in_5,
  input  [31:0] in_6,
  input  in_7,
  input  in_8,
  input  [31:0] in_9,
  input  in_10,
  input  in_11,
  input  in_12,
  input  [31:0] HI,
  input  in_14,
  input  in_15,
  input  [31:0] LO,
  input  in_17,
  input  [4:0] in_18,
  input  [4:0] in_19,
  input  [4:0] in_20,
  output [31:0] Output,
  output [31:0] Output_2,
  output [31:0] Output_3
);

  wire input31, L0, L1, L2, L3, L4, L5, L6, L7, L8, L9, L10, L11, L12, L13, L14, L15, L16, L17, L18, L19,
       L20, L21, L22, L23, L24, L25, L26, L27, L28, L29, L30, L31, or_4_out, or_5_out;
  wire [2:0] selector;
  wire [31:0] adder_1_out, \input , KBD, multiplexer_4_out, multiplexer_6_out, out0, out1, out2, out3, out4,
       out5, out6, out7, out8, out9, out10, out11, out12, out13, out14, out15, out16, out17, out18, out19,
       out20, out21, out22, out23, out24, out25, out26, out27, out28, out29, out30, SP, subtractor_1_out;

  Register #(.width(32)) register_1 (.D({32{1'b0}}), .en(L0), .Q(out0), .clk(in_15), .clr(in_14));
  Register #(.width(32)) register_2 (.D(\input ), .en(L8), .Q(out8), .clk(in_15), .clr(in_14));
  Register #(.width(32)) register_3 (.D(\input ), .en(L16), .Q(out16), .clk(in_15), .clr(in_14));
  Register #(.width(32)) register_4 (.D(\input ), .en(L24), .Q(out24), .clk(in_15), .clr(in_14));
  Demultiplexer #(.select(5), .enable("false")) demultiplexer_1 (
    .out0(L0), .out1(L1), .out2(L2), .out3(L3), .out4(L4), .out5(L5), .out6(L6), .out7(L7), .out8(L8),
    .out9(L9), .out10(L10), .out11(L11), .out12(L12), .out13(L13), .out14(L14), .out15(L15), .out16(L16),
    .out17(L17), .out18(L18), .out19(L19), .out20(L20), .out21(L21), .out22(L22), .out23(L23), .out24(L24),
    .out25(L25), .out26(L26), .out27(L27), .out28(L28), .out29(L29), .out30(L30), .out31(input31),
    .in(in_17), .sel(in_18));
  Register #(.width(32)) register_5 (.D(\input ), .en(L1), .Q(out1), .clk(in_15), .clr(in_14));
  Register #(.width(32)) register_6 (.D(\input ), .en(L9), .Q(out9), .clk(in_15), .clr(in_14));
  Register #(.width(32)) register_7 (.D(\input ), .en(L17), .Q(out17), .clk(in_15), .clr(in_14));
  Register #(.width(32)) register_8 (.D(\input ), .en(L25), .Q(out25), .clk(in_15), .clr(in_14));
  Multiplexer #(.select(5), .width(32), .enable("false")) multiplexer_1 (
    .in0(out0), .in1(out1), .in2(out2), .in3(out3), .in4(out4), .in5(out5), .in6(out6), .in7(out7),
    .in8(out8), .in9(out9), .in10(out10), .in11(out11), .in12(out12), .in13(out13), .in14(out14),
    .in15(out15), .in16(out16), .in17(out17), .in18(out18), .in19(out19), .in20(out20), .in21(out21),
    .in22(out22), .in23(out23), .in24(out24), .in25(out25), .in26(out26), .in27(out27), .in28(out28),
    .in29(out29), .in30(out30), .in31(Output_3), .out(Output), .sel(in_19));
  Register #(.width(32)) register_9 (.D(\input ), .en(L2), .Q(out2), .clk(in_15), .clr(in_14));
  Register #(.width(32)) register_10 (.D(\input ), .en(L10), .Q(out10), .clk(in_15), .clr(in_14));
  Register #(.width(32)) register_11 (.D(\input ), .en(L18), .Q(out18), .clk(in_15), .clr(in_14));
  Register #(.width(32)) register_12 (.D(\input ), .en(L26), .Q(out26), .clk(in_15), .clr(in_14));
  or or_1 (selector[0], in_3, in_4, in_7, in_10);
  or or_2 (selector[1], in_5, in_7);
  or or_3 (selector[2], in_8, in_10);
  Multiplexer #(.select(3), .width(32), .enable("false")) multiplexer_2 (
    .in0(in_2), .in1(in_9), .in2(HI), .in3(LO), .in4(in_6), .in5(KBD), .out(\input ), .sel(selector));  // open: in6, in7
  Register #(.width(32)) register_13 (.D(\input ), .en(L3), .Q(out3), .clk(in_15), .clr(in_14));
  Register #(.width(32)) register_14 (.D(\input ), .en(L11), .Q(out11), .clk(in_15), .clr(in_14));
  Register #(.width(32)) register_15 (.D(\input ), .en(L19), .Q(out19), .clk(in_15), .clr(in_14));
  Register #(.width(32)) register_16 (.D(\input ), .en(L27), .Q(out27), .clk(in_15), .clr(in_14));
  Multiplexer #(.select(5), .width(32), .enable("false")) multiplexer_3 (
    .in0(out0), .in1(out1), .in2(out2), .in3(out3), .in4(out4), .in5(out5), .in6(out6), .in7(out7),
    .in8(out8), .in9(out9), .in10(out10), .in11(out11), .in12(out12), .in13(out13), .in14(out14),
    .in15(out15), .in16(out16), .in17(out17), .in18(out18), .in19(out19), .in20(out20), .in21(out21),
    .in22(out22), .in23(out23), .in24(out24), .in25(out25), .in26(out26), .in27(out27), .in28(out28),
    .in29(out29), .in30(out30), .in31(Output_3), .out(Output_2), .sel(in_20));
  Register #(.width(32)) register_17 (.D(\input ), .en(L4), .Q(out4), .clk(in_15), .clr(in_14));
  Register #(.width(32)) register_18 (.D(\input ), .en(L12), .Q(out12), .clk(in_15), .clr(in_14));
  Register #(.width(32)) register_19 (.D(\input ), .en(L20), .Q(out20), .clk(in_15), .clr(in_14));
  Register #(.width(32)) register_20 (.D(\input ), .en(L28), .Q(out28), .clk(in_15), .clr(in_14));
  Register #(.width(32)) register_21 (.D(\input ), .en(L5), .Q(out5), .clk(in_15), .clr(in_14));
  Register #(.width(32)) register_22 (.D(\input ), .en(L13), .Q(out13), .clk(in_15), .clr(in_14));
  Register #(.width(32)) register_23 (.D(\input ), .en(L21), .Q(out21), .clk(in_15), .clr(in_14));
  Register #(.width(32)) register_24 (.D(\input ), .en(L29), .Q(out29), .clk(in_15), .clr(in_14));
  or or_4 (or_4_out, in_11, in_4);
  Subtractor #(.width(32)) subtractor_1 (.a(Output_3), .b(32'h4), .out(subtractor_1_out));  // open: bin, bout
  Adder #(.width(32)) adder_1 (.a(32'h4), .b(Output_3), .out(adder_1_out));  // open: cin, cout
  Register #(.width(32)) register_25 (.D(\input ), .en(L6), .Q(out6), .clk(in_15), .clr(in_14));
  Register #(.width(32)) register_26 (.D(\input ), .en(L14), .Q(out14), .clk(in_15), .clr(in_14));
  Register #(.width(32)) register_27 (.D(\input ), .en(L22), .Q(out22), .clk(in_15), .clr(in_14));
  Register #(.width(32)) register_28 (.D(\input ), .en(L30), .Q(out30), .clk(in_15), .clr(in_14));
  and and_1 (L31, in_12, or_4_out);
  Multiplexer #(.width(32), .enable("false")) multiplexer_4 (
    .in0(subtractor_1_out), .in1(adder_1_out), .out(multiplexer_4_out), .sel(in_4));
  Multiplexer #(.width(32), .enable("false")) multiplexer_5 (
    .in0(multiplexer_4_out), .in1({32{1'b1}}), .out(SP), .sel(in_14));
  Register #(.width(32)) register_29 (.D(\input ), .en(L7), .Q(out7), .clk(in_15), .clr(in_14));
  Register #(.width(32)) register_30 (.D(\input ), .en(L15), .Q(out15), .clk(in_15), .clr(in_14));
  Register #(.width(32)) register_31 (.D(\input ), .en(L23), .Q(out23), .clk(in_15), .clr(in_14));
  Multiplexer #(.width(32), .enable("false")) multiplexer_6 (
    .in0(SP), .in1(\input ), .out(multiplexer_6_out), .sel(input31));
  Register #(.width(32)) register_32 (.D(multiplexer_6_out), .en(or_5_out), .Q(Output_3), .clk(in_15));  // open: clr
  or or_5 (or_5_out, L31, input31, in_14);

  // Other names for the same wires on the sheet: A[31:0] = Output; ALU[31:0] = in_2; B[31:0] = Output_2;
  //   clock = in_15; flag_kbd = in_10; flag_rnd = in_8; lw = in_3; MA[31:0] = in_9; memR_W = in_12; mfhi = in_5;
  //   mflo = in_7; out31[31:0] = Output_3; outA[4:0] = in_19; outB[4:0] = in_20; pop = in_4; push = in_11;
  //   reset = in_14; RND[31:0] = in_6; select[4:0] = in_18; write = in_17
endmodule

module Instruction_Decoder (
  input  [31:0] Instruction,
  output [4:0] RS,
  output [4:0] RT,
  output [4:0] RD,
  output [25:0] Destine,
  output [15:0] Constant,
  output [5:0] Op_code,
  output [5:0] Func_code
);


  assign Constant = Instruction[15:0];
  assign Destine = Instruction[25:0];
  assign Func_code = Instruction[5:0];
  assign Op_code = Instruction[31:26];
  assign RD = Instruction[15:11];
  assign RS = Instruction[25:21];
  assign RT = Instruction[20:16];

  // Other names for the same wires on the sheet: Jump[25:0] = Instruction[25:0]
endmodule

module Memory_Address (
  input  [31:0] Program_Counter,
  input  [31:0] Stack_Pointer,
  input  [31:0] ALU_Result,
  input  Pop,
  input  Push,
  input  Lw,
  input  Sw,
  output [31:0] Address
);

  wire or_1_out, or_2_out;
  wire [31:0] multiplexer_1_out;

  Multiplexer #(.width(32), .enable("false")) multiplexer_1 (
    .in0(Program_Counter), .in1(ALU_Result), .out(multiplexer_1_out), .sel(or_1_out));
  or or_1 (or_1_out, Lw, Sw);
  Multiplexer #(.width(32), .enable("false")) multiplexer_2 (
    .in0(multiplexer_1_out), .in1(Stack_Pointer), .out(Address), .sel(or_2_out));
  or or_2 (or_2_out, Push, Pop);

  // Other names for the same wires on the sheet: ALU[31:0] = ALU_Result; Out[31:0] = Address;
  //   PC[31:0] = Program_Counter; SP[31:0] = Stack_Pointer
endmodule

module Instruction (
  input  [31:0] Input,
  input  CLK,
  input  RST,
  input  EN,
  output [31:0] Output
);

  Register #(.width(32)) register_1 (
    .D(Input), .en(EN), .Q({Output[7:0], Output[15:8], Output[23:16], Output[31:24]}), .clk(CLK), .clr(RST));

  // Other names for the same wires on the sheet: In[31:0] = Input; Out[31:0] = Output
endmodule

module Program_Counter (
  input  [31:0] Input,
  input  Clock,
  input  Reset,
  input  Enable,
  output [31:0] Output
);

  Register #(.width(32)) register_1 (.D(Input), .en(Enable), .Q(Output), .clk(Clock), .clr(Reset));
endmodule

module Branch_Control (
  input  [31:0] Instruction_Address,
  input  [25:0] Destine,
  input  [15:0] Offset,
  input  [31:0] RS,
  input  [31:0] RT,
  input  [5:0] Op_code,
  input  [5:0] Func_code,
  output [31:0] Next_Instruction_Address
);

  wire and_2_out, and_3_out, and_4_out, and_5_out, and_6_out, beq, bgtz, blez, bltz, bne, comparator_7_eq,
       comparator_8_eq, equal, ez, FCond, FJ, FJr, gtz, ltz, or_1_out;
  wire [13:0] bit_extender_1_out;
  wire [31:0] multiplexer_1_out, multiplexer_2_out, PC_4, PC_4_4_offset;

  Adder #(.width(32)) adder_1 (.a(Instruction_Address), .b(32'h4), .out(PC_4));  // open: cin, cout
  assign bit_extender_1_out = {{13{Offset[15]}}, Offset[15]};  // Bit_Extender bit_extender_1
  Comparator_part #(.width(6)) comparator_1 (.a(Op_code), .b(6'b000100), .eq(beq));  // open: gt, lt
  Comparator_part #(.width(6)) comparator_2 (.a(Op_code), .b(6'b000101), .eq(bne));  // open: gt, lt
  Comparator_part #(.width(6)) comparator_3 (.a(Op_code), .b(6'b000110), .eq(blez));  // open: gt, lt
  Comparator_part #(.width(6)) comparator_4 (.a(Op_code), .b(6'b000111), .eq(bgtz));  // open: gt, lt
  Comparator_part #(.width(6)) comparator_5 (.a(Op_code), .b(6'b000001), .eq(bltz));  // open: gt, lt
  Comparator_part #(.width(6)) comparator_6 (.a(Op_code), .b(6'b000010), .eq(FJ));  // open: gt, lt
  Comparator_part #(.width(6)) comparator_7 (.a(Op_code), .b({6{1'b0}}), .eq(comparator_7_eq));  // open: gt, lt
  Comparator_part #(.width(6)) comparator_8 (.a(Func_code), .b(6'b001000), .eq(comparator_8_eq));  // open: gt, lt
  and and_1 (FJr, comparator_7_eq, comparator_8_eq);
  Adder #(.width(32)) adder_2 (
    .a(PC_4), .b({bit_extender_1_out, Offset, 2'b00}), .out(PC_4_4_offset));  // open: cin, cout
  and and_2 (and_2_out, ltz, bltz);
  and and_3 (and_3_out, gtz, bgtz);
  or or_1 (or_1_out, ez, ltz);
  and and_4 (and_4_out, or_1_out, blez);
  and and_5 (and_5_out, ~equal, bne);  // AND_Gate
  and and_6 (and_6_out, equal, beq);
  or or_2 (FCond, and_2_out, and_3_out, and_4_out, and_5_out, and_6_out);
  Multiplexer #(.width(32), .enable("false")) multiplexer_1 (
    .in0(PC_4), .in1(PC_4_4_offset), .out(multiplexer_1_out), .sel(FCond));
  Comparator_part #(.width(32)) comparator_9 (.a(RS), .b(RT), .eq(equal));  // open: gt, lt
  Comparator_part #(.width(32)) comparator_10 (.a(RS), .b({32{1'b0}}), .gt(gtz), .eq(ez), .lt(ltz));
  Multiplexer #(.width(32), .enable("false")) multiplexer_2 (
    .in0(multiplexer_1_out), .in1(RS), .out(multiplexer_2_out), .sel(FJr));
  Multiplexer #(.width(32), .enable("false")) multiplexer_3 (
    .in0(multiplexer_2_out), .in1({Instruction_Address[31:28], Destine, 2'b00}),
    .out(Next_Instruction_Address), .sel(FJ));

  // Other names for the same wires on the sheet: IA_prime[31:0] = Next_Instruction_Address; Dest[25:0] = Destine;
  //   Jump[31:2] = {Instruction_Address[31:28], Destine}; PC[31:0] = Instruction_Address
endmodule

module Memory_Control (
  input  [3:0] in_1,
  input  [3:0] in_2,
  input  in_3,
  input  in_4,
  input  [31:0] in_5,
  input  in_6,
  input  in_7,
  input  in_8,
  input  in_9,
  input  [31:0] in_10,
  input  [31:0] in_11,
  input  [31:0] in_12,
  input  [31:0] in_13,
  output [31:0] Output,
  output [31:0] Output_2,
  output [31:0] Output_3,
  output [31:0] Output_4,
  output [15:0] Output_5,
  output [3:0] Output_6,
  output Output_7,
  output Output_8,
  output Output_9,
  output Output_10,
  output Output_11
);

  wire CSD, CSI, or_1_out, stop;
  wire [31:0] DO0, DO1, DO2, DO3, IO0, IO1, IO2, IO3;

  or or_1 (or_1_out, in_6, stop);
  RAM_Read ram_read_1 (
    .in_5(in_5), .in_6(in_10), .in_7(in_11), .in_8(in_12), .in_1(in_1), .in_3(in_4), .in_4(in_7),
    .Output_3(IO0), .Output_4(IO1), .Output_5(IO2), .Output_6(IO3), .Output(CSI), .Output_2(Output_9),
    .in_2(in_3));
  D_Flip_Flop #(.trigger("falling")) d_ff_1 (
    .clk(in_3), .D(in_6), .Q(Output_8), .en(or_1_out));  // open: Qn, preset, reset
  Delay delay_1 (.in_1(Output_8), .in_2(Output_11), .in_3(in_3), .in_4(in_2), .Output(stop));
  Multiplexer #(.width(32), .enable("false")) multiplexer_1 (
    .in0({DO0[7:0], DO0[15:8], DO0[23:16], DO0[31:24]}), .in1(IO0), .out(Output), .sel(in_9));
  Multiplexer #(.width(32), .enable("false")) multiplexer_2 (
    .in0({DO2[7:0], DO2[15:8], DO2[23:16], DO2[31:24]}), .in1(IO2), .out(Output_3), .sel(in_9));
  RAM_Read ram_read_2 (
    .in_5(in_5), .in_6(in_10), .in_7(in_11), .in_8(in_12), .in_1(in_1), .in_3(in_4), .in_4(in_8),
    .Output_3(DO0), .Output_4(DO1), .Output_5(DO2), .Output_6(DO3), .Output(CSD), .Output_2(Output_10),
    .in_2(in_3));
  D_Flip_Flop #(.trigger("falling")) d_ff_2 (.clk(in_3), .D(stop), .Q(Output_11));  // open: Qn, preset, en, reset
  Multiplexer #(.width(32), .enable("false")) multiplexer_3 (
    .in0({DO1[7:0], DO1[15:8], DO1[23:16], DO1[31:24]}), .in1(IO1), .out(Output_2), .sel(in_9));
  Multiplexer #(.width(32), .enable("false")) multiplexer_4 (
    .in0({DO3[7:0], DO3[15:8], DO3[23:16], DO3[31:24]}), .in1(IO3), .out(Output_4), .sel(in_9));
  Demultiplexer #(.select(2), .enable("false")) demultiplexer_1 (
    .out0(Output_6[0]), .out1(Output_6[1]), .out2(Output_6[2]), .out3(Output_6[3]), .in(1'b1),
    .sel(in_13[3:2]));
  or or_2 (Output_7, CSD, CSI, Output_8);

  assign Output_5 = in_13[19:4];

  // Other names for the same wires on the sheet: bank0[31:0] = in_5; bank1[31:0] = in_10; bank2[31:0] = in_11;
  //   bank3[31:0] = in_12; clock = in_3; CS = Output_7; DP_address[31:0] = in_13; ADDR[15:0] = in_13[19:4];
  //   get_data = in_8; get_inst = in_7; is_inst = in_9; MASK[3:0] = Output_6; out_bank0[31:0] = Output;
  //   out_bank1[31:0] = Output_2; out_bank2[31:0] = Output_3; out_bank3[31:0] = Output_4; read_time[3:0] = in_1;
  //   ready_data = Output_10; ready_inst = Output_9; ready_write = Output_11; reset = in_4; RW = Output_8;
  //   write = in_6; write_time[3:0] = in_2
endmodule

module RAM_Read (
  input  [3:0] in_1,
  input  in_2,
  input  in_3,
  input  in_4,
  input  [31:0] in_5,
  input  [31:0] in_6,
  input  [31:0] in_7,
  input  [31:0] in_8,
  output Output,
  output Output_2,
  output [31:0] Output_3,
  output [31:0] Output_4,
  output [31:0] Output_5,
  output [31:0] Output_6
);

  wire a, enable, or_1_out, stop;

  D_Flip_Flop #(.trigger("falling")) d_ff_1 (.clk(in_2), .D(in_4), .Q(a), .en(or_1_out));  // open: Qn, preset, reset
  or or_1 (or_1_out, in_4, stop);
  Delay delay_1 (.in_1(a), .in_2(Output_2), .in_3(in_2), .in_4(in_1), .Output(stop));
  Register #(.width(32)) register_1 (.D(in_5), .en(enable), .Q(Output_3), .clk(in_2), .clr(in_3));
  Register #(.width(32)) register_2 (.D(in_7), .en(enable), .Q(Output_5), .clk(in_2), .clr(in_3));
  or or_2 (Output, a, enable);
  D_Flip_Flop #(.trigger("falling")) d_ff_2 (
    .clk(in_2), .D(stop), .Q(enable), .reset(Output_2));  // open: Qn, preset, en
  Register #(.width(32)) register_3 (.D(in_6), .en(enable), .Q(Output_4), .clk(in_2), .clr(in_3));
  Register #(.width(32)) register_4 (.D(in_8), .en(enable), .Q(Output_6), .clk(in_2), .clr(in_3));
  D_Flip_Flop #(.trigger("falling")) d_ff_3 (.clk(in_2), .D(enable), .Q(Output_2));  // open: Qn, preset, en, reset

  // Other names for the same wires on the sheet: bank0[31:0] = in_5; bank1[31:0] = in_6; bank2[31:0] = in_7;
  //   bank3[31:0] = in_8; chip_select = Output; clock = in_2; get = in_4; out_bank0[31:0] = Output_3;
  //   out_bank1[31:0] = Output_4; out_bank2[31:0] = Output_5; out_bank3[31:0] = Output_6; read_time[3:0] = in_1;
  //   ready = Output_2; reset = in_3
endmodule

module Delay (
  input  in_1,
  input  in_2,
  input  in_3,
  input  [3:0] in_4,
  output Output
);

  wire [3:0] counter_1_q;

  Counter #(.width(4), .max('hf)) counter_1 (
    .count(in_1), .Q(counter_1_q), .clk(in_3), .clr(in_2));  // open: load, D, carry
  Comparator_part #(.width(4)) comparator_1 (.a(in_4), .b(counter_1_q), .eq(Output));  // open: gt, lt

  // Other names for the same wires on the sheet: clock = in_3; ready = Output; reset = in_2; start = in_1;
  //   wait_time[3:0] = in_4
endmodule
